# Fritzing sketch MIDI_IN_new (saved by Fritzing 0.9.3b)
breadboards: 1

parts:
  Part1 = Arduino Uno (Rev3)
  DIN1 = DIN-5 jack (MIDI) [package=THT]
  IC1 = IC, DIP package, 8 pins [chip_label=6n138]
  D1 = Rectifier Diode [part_number=1N4148 package="300 mil [THT]"]
  R2 = Resistor [tolerance=±5% resistance=220 package=THT]
  R3 = Resistor [tolerance=±5% resistance=220 package=THT]

nets:
  N1: Part1.D11_PWM/MOSI, IC1.pin6, R3.Pin_1
  N2: Part1.5V, IC1.pin8, R3.Pin_0
  N3: Part1.GND, IC1.pin5
  N4: DIN1.5, R2.Pin_1
  N5: DIN1.4, IC1.pin2, D1.cathode
  N6: IC1.pin3, D1.anode, R2.Pin_0

notes:
  front view
