# Fritzing sketch MIDI_OUT_new (saved by Fritzing 0.9.3b)
breadboards: 1

parts:
  Part1 = Arduino Uno (Rev3)
  DIN2 = DIN-5 jack (MIDI) [package=THT]
  R4 = Resistor [tolerance=±5% resistance=220 package=THT]
  R5 = Resistor [tolerance=±5% resistance=220 package=THT]

nets:
  N1: Part1.D10_PWM/SS, R4.Pin_1
  N2: Part1.5V, R5.Pin_1
  N3: Part1.GND, DIN2.2
  N4: DIN2.5, R4.Pin_0
  N5: DIN2.4, R5.Pin_0

notes:
  front view
