# Fritzing sketch photoresistor-02 (saved by Fritzing 0.9.3b)
breadboards: 1

parts:
  Part1 = Arduino Uno (Rev3)
  R1 = Photocell (LDR) [package=THT]
  R2 = Resistor [tolerance=±5% resistance=1k package=THT]
  C1 = Electrolytic Capacitor [capacitance=0.1mF package="100 mil [THT, electrolytic]"]
  R3 = Resistor [tolerance=±10% resistance=1.5k package=THT]

nets:
  N1: Part1.A0, C1.+, R3.Pin_1
  N2: Part1.A5/SCL, R1.pin_0, R2.Pin_1, R3.Pin_0
  N3: Part1.5V, R2.Pin_0
  N4: Part1.GND, R1.pin_1, C1.-

notes:
  Va
  Vb
